// Logisim project Lab1.circ as structural Verilog: 1 circuit, main circuit main
module main (
  input  in_1,
  input  in_2,
  input  A,
  input  in_4,
  input  S0,
  input  S1,
  input  S2,
  input  S3,
  input  A1,
  input  B1,
  input  S,
  input  [7:0] in_12,
  input  in_13,
  input  As,
  input  in_15,
  input  in_16,
  input  in_17,
  input  Bs,
  input  [7:0] in_19,
  input  Cin,
  input  in_21,
  input  in_22,
  input  in_23,
  output out_24,
  output out_25,
  output out_26,
  output [7:0] out_27,
  output Sum,
  output out_29,
  output out_30,
  output Cout,
  output out_32,
  output out_33,
  output out_34
);

  wire and_1_out, and_2_out, and_3_out, and_4_out, and_5_out, and_6_out, and_7_out, and_8_out, and_9_out,
       and_10_out, and_11_out, and_12_out, and_13_out, and_14_out, and_15_out, and_16_out, and_17_out,
       and_18_out, and_19_out, and_20_out, and_21_out, and_22_out, and_23_out, and_24_out, and_25_out,
       and_26_out, and_27_out, and_28_out, and_29_out, and_30_out, not_1_out, not_2_out, not_3_out,
       not_4_out, not_5_out, or_1_out, or_2_out, or_7_out, or_10_out, or_11_out, or_12_out, or_13_out,
       or_14_out, or_15_out, or_16_out, or_17_out, or_18_out, or_19_out, or_20_out, or_21_out, or_22_out,
       or_23_out, or_24_out, xor_1_out, xor_2_out, xor_5_out, xor_7_out, xor_8_out, xor_9_out, xor_10_out,
       xor_11_out, xor_12_out, xor_13_out, xor_14_out;

  not not_1 (not_1_out, A);
  and and_1 (and_1_out, Bs, As);
  xor xor_1 (xor_1_out, in_21, in_22);
  and and_2 (and_2_out, in_22, in_21);
  or or_1 (or_1_out, in_22, in_21);
  not not_2 (not_2_out, S);
  xor xor_2 (xor_2_out, As, Bs);
  or or_2 (or_2_out, Bs, As);
  xor xor_3 (out_32, xor_1_out, in_23);
  or or_3 (out_33, and_2_out, and_3_out);
  and and_3 (and_3_out, or_1_out, in_23);
  and and_4 (and_4_out, or_2_out, Cin);
  not not_3 (not_3_out, in_4);
  and and_5 (and_5_out, A1, not_2_out);
  and and_6 (and_6_out, B1, S);
  xor xor_4 (Sum, xor_2_out, Cin);
  or or_4 (Cout, and_1_out, and_4_out);
  and and_7 (and_7_out, A, not_3_out);
  and and_8 (and_8_out, not_1_out, in_4);
  or or_5 (out_26, and_5_out, and_6_out);
  or or_6 (out_24, and_7_out, and_8_out);
  and and_9 (and_9_out, in_16, in_15);
  or or_7 (or_7_out, in_16, in_15);
  xor xor_5 (xor_5_out, in_15, in_16);
  and and_10 (and_10_out, or_7_out, in_17);
  xor xor_6 (out_29, xor_5_out, in_17);
  or or_8 (out_30, and_9_out, and_10_out);
  not not_4 (not_4_out, in_1);
  not not_5 (not_5_out, in_2);
  and and_11 (and_11_out, S0, not_4_out, not_5_out);
  and and_12 (and_12_out, S1, not_4_out, in_2);
  and and_13 (and_13_out, S2, in_1, not_5_out);
  and and_14 (and_14_out, S3, in_1, in_2);
  or or_9 (out_25, and_11_out, and_12_out, and_13_out, and_14_out);
  and and_15 (and_15_out, in_19[0], in_12[0]);
  or or_10 (or_10_out, in_19[0], in_12[0]);
  and and_16 (and_16_out, in_19[1], in_12[1]);
  or or_11 (or_11_out, in_19[1], in_12[1]);
  and and_17 (and_17_out, in_19[3], in_12[3]);
  or or_12 (or_12_out, in_19[3], in_12[3]);
  xor xor_7 (xor_7_out, in_12[0], in_19[0]);
  and and_18 (and_18_out, or_10_out, in_13);
  xor xor_8 (xor_8_out, in_12[1], in_19[1]);
  and and_19 (and_19_out, or_11_out, or_18_out);
  xor xor_9 (xor_9_out, in_12[2], in_19[2]);
  and and_20 (and_20_out, in_19[2], in_12[2]);
  or or_13 (or_13_out, in_19[2], in_12[2]);
  and and_21 (and_21_out, or_13_out, or_19_out);
  xor xor_10 (xor_10_out, in_12[3], in_19[3]);
  and and_22 (and_22_out, or_12_out, or_20_out);
  xor xor_11 (xor_11_out, in_12[4], in_19[4]);
  and and_23 (and_23_out, in_19[4], in_12[4]);
  or or_14 (or_14_out, in_19[4], in_12[4]);
  and and_24 (and_24_out, or_14_out, or_21_out);
  xor xor_12 (xor_12_out, in_12[5], in_19[5]);
  and and_25 (and_25_out, in_19[5], in_12[5]);
  or or_15 (or_15_out, in_19[5], in_12[5]);
  and and_26 (and_26_out, or_15_out, or_22_out);
  xor xor_13 (xor_13_out, in_12[6], in_19[6]);
  and and_27 (and_27_out, in_19[6], in_12[6]);
  or or_16 (or_16_out, in_19[6], in_12[6]);
  xor xor_14 (xor_14_out, in_12[7], in_19[7]);
  and and_28 (and_28_out, in_19[7], in_12[7]);
  or or_17 (or_17_out, in_19[7], in_12[7]);
  and and_29 (and_29_out, or_17_out, or_24_out);
  xor xor_15 (out_27[0], xor_7_out, in_13);
  or or_18 (or_18_out, and_15_out, and_18_out);
  xor xor_16 (out_27[1], xor_8_out, or_18_out);
  or or_19 (or_19_out, and_16_out, and_19_out);
  xor xor_17 (out_27[2], xor_9_out, or_19_out);
  or or_20 (or_20_out, and_20_out, and_21_out);
  xor xor_18 (out_27[3], xor_10_out, or_20_out);
  or or_21 (or_21_out, and_17_out, and_22_out);
  xor xor_19 (out_27[4], xor_11_out, or_21_out);
  or or_22 (or_22_out, and_23_out, and_24_out);
  xor xor_20 (out_27[5], xor_12_out, or_22_out);
  or or_23 (or_23_out, and_25_out, and_26_out);
  xor xor_21 (out_27[6], xor_13_out, or_23_out);
  or or_24 (or_24_out, and_27_out, and_30_out);
  and and_30 (and_30_out, or_16_out, or_23_out);
  xor xor_22 (out_27[7], xor_14_out, or_24_out);
  or or_25 (out_34, and_28_out, and_29_out);

  // Notes on the sheet:
  //   B
  //   CIRCUITO SUMADOR ADD1
  //   CIRCUITO XOR
  //   CIRCUITO MUX2
  //   A*¬B
  //   ¬A*B
  //   A*¬B + ¬A*B
  //   CIRCUITO MUX4
endmodule
